// Logisim project project1.circ as structural Verilog: 18 circuits, main circuit main
module main (
  input  [3:0] LSB,
  input  [3:0] LSB_2
);

  wire Div_Lights_div_by_2, Div_Lights_div_by_3, Div_Lights_div_by_4, ones_7_segment_1_a, ones_7_segment_1_b,
       ones_7_segment_1_c, ones_7_segment_1_d, ones_7_segment_1_e, ones_7_segment_1_f, ones_7_segment_1_g,
       tens_7_segment_1_a, tens_7_segment_1_b, tens_7_segment_1_c, tens_7_segment_1_d, tens_7_segment_1_e,
       tens_7_segment_1_f, tens_7_segment_1_g;
  wire [3:0] adder_1_out;
  wire [4:4] adder_1_cout;

  Adder #(.width(4)) adder_1 (.a(LSB), .b(LSB_2), .out(adder_1_out), .cout(adder_1_cout[4]));  // open: cin
  LED Div_by_4 (.in(Div_Lights_div_by_4));
  Div_Lights Div_Lights (
    .in_1({adder_1_cout[4], adder_1_out}), .Div_by_4(Div_Lights_div_by_4), .Div_by_3(Div_Lights_div_by_3),
    .Div_by_2(Div_Lights_div_by_2));
  LED Div_by_3 (.in(Div_Lights_div_by_3));
  LED Div_by_2 (.in(Div_Lights_div_by_2));
  _7_Segment_Display u_7_segment_display_1 (
    .g(tens_7_segment_1_g), .f(tens_7_segment_1_f), .a(tens_7_segment_1_a), .b(tens_7_segment_1_b),
    .e(tens_7_segment_1_e), .d(tens_7_segment_1_d), .c(tens_7_segment_1_c));  // open: dp
  Tens_7_segment tens_7_segment_1 (
    .in_1({adder_1_cout[4], adder_1_out}), .a(tens_7_segment_1_a), .b(tens_7_segment_1_b),
    .c(tens_7_segment_1_c), .d(tens_7_segment_1_d), .e(tens_7_segment_1_e), .f(tens_7_segment_1_f),
    .g(tens_7_segment_1_g));
  _7_Segment_Display u_7_segment_display_2 (
    .g(ones_7_segment_1_g), .f(ones_7_segment_1_f), .a(ones_7_segment_1_a), .b(ones_7_segment_1_b),
    .e(ones_7_segment_1_e), .d(ones_7_segment_1_d), .c(ones_7_segment_1_c));  // open: dp
  Ones_7_segment ones_7_segment_1 (
    .in_1({adder_1_cout[4], adder_1_out}), .a(ones_7_segment_1_a), .b(ones_7_segment_1_b),
    .c(ones_7_segment_1_c), .d(ones_7_segment_1_d), .e(ones_7_segment_1_e), .f(ones_7_segment_1_f),
    .g(ones_7_segment_1_g));

  // Notes on the sheet:
  //   MSB
  //   Input A
  //   Input B
  //   MSB
  //   Adder with Divisibility Indicator
  //   Tens
  //   Ones
endmodule

module Tens_7_segment (
  input  [4:0] in_1,
  output a,
  output b,
  output c,
  output d,
  output e,
  output f,
  output g
);

  a__Tens_7_seg u_A (.MSB(in_1[4]), .in_2(in_1[3]), .in_3(in_1[2]), .in_4(in_1[1]), .LSB(in_1[0]), .out_6(a));
  c__Tens_7_seg u_C (.MSB(in_1[4]), .D(in_1[3]), .C(in_1[2]), .in_4(in_1[1]), .LSB(in_1[0]), .out_6(c));
  d__Tens_7_seg u_D (.MSB(in_1[4]), .D(in_1[3]), .C(in_1[2]), .B(in_1[1]), .LSB(in_1[0]), .out_6(d));
  e__Tens_7_seg u_E (.MSB(in_1[4]), .D(in_1[3]), .C(in_1[2]), .in_4(in_1[1]), .LSB(in_1[0]), .out_6(e));
  f__Tens_7_seg u_F (.MSB(in_1[4]), .D(in_1[3]), .C(in_1[2]), .B(in_1[1]), .LSB(in_1[0]), .out_6(f));
  g__Tens_7_seg u_G (.MSB(in_1[4]), .in_2(in_1[3]), .in_3(in_1[2]), .in_4(in_1[1]), .LSB(in_1[0]), .E_D_C(g));

  assign b = 1'b1;

  // Notes on the sheet:
  //   E
  //   D
  //   C
  //   B
  //   A
  //   Tens 7-segment
  //   Subcircuit
endmodule

module Ones_7_segment (
  input  [4:0] in_1,
  output a,
  output b,
  output c,
  output d,
  output e,
  output f,
  output g
);

  a__Ones_7_seg u_A (.MSB(in_1[4]), .in_2(in_1[3]), .in_3(in_1[2]), .in_4(in_1[1]), .LSB(in_1[0]), .out_6(a));
  b__Ones_7_seg u_B (.MSB(in_1[4]), .in_2(in_1[3]), .in_3(in_1[2]), .in_4(in_1[1]), .LSB(in_1[0]), .out_6(b));
  c__Ones_7_seg u_C (.MSB(in_1[4]), .D(in_1[3]), .in_3(in_1[2]), .in_4(in_1[1]), .LSB(in_1[0]), .out_6(c));
  d__Ones_7_seg u_D (.MSB(in_1[4]), .in_2(in_1[3]), .in_3(in_1[2]), .in_4(in_1[1]), .LSB(in_1[0]), .out_6(d));
  e__Ones_7_seg u_E (.MSB(in_1[4]), .in_2(in_1[3]), .in_3(in_1[2]), .in_4(in_1[1]), .LSB(in_1[0]), .out_6(e));
  f__Ones_7_seg u_F (.MSB(in_1[4]), .in_2(in_1[3]), .in_3(in_1[2]), .in_4(in_1[1]), .LSB(in_1[0]), .out_6(f));
  g__Ones_7_seg u_G (.MSB(in_1[4]), .D(in_1[3]), .C(in_1[2]), .in_4(in_1[1]), .LSB(in_1[0]), .out_6(g));

  // Notes on the sheet:
  //   D
  //   E
  //   C
  //   B
  //   A
  //   Ones 7-segment
  //   Subcircuit
endmodule

module Div_Lights (
  input  [4:0] in_1,
  output Div_by_4,
  output Div_by_3,
  output Div_by_2
);

  nor nor_1 (Div_by_4, in_1[0], in_1[1]);
  Div_By_3 Div_by_3_Circuit (
    .out_6(Div_by_3), .MSB(in_1[4]), .in_2(in_1[3]), .in_3(in_1[2]), .in_4(in_1[1]), .LSB(in_1[0]));
  not not_1 (Div_by_2, in_1[0]);
endmodule

module Div_By_3 (
  input  MSB,
  input  in_2,
  input  in_3,
  input  in_4,
  input  LSB,
  output out_6
);

  wire and_1_out, and_2_out, D_prime_C_prime_B_prime_A_prime_out, D_prime_C_prime_BA_out,
       D_prime_C_prime_BA_prime_out, D_prime_CB_prime_A_out, D_prime_CBA_prime_out, DC_prime_B_prime_A_out,
       DC_prime_B_prime_A_prime_out, DC_prime_BA_out, DCB_prime_A_prime_out, DCBA_out, DCBA_prime_out,
       not_1_out, not_2_out, not_3_out, not_4_out, not_5_out, or_1_out, or_2_out, or_3_out;

  not not_1 (not_1_out, MSB);
  not not_2 (not_2_out, in_2);
  not not_3 (not_3_out, in_3);
  not not_4 (not_4_out, in_4);
  not not_5 (not_5_out, LSB);
  and DCB_prime_A_prime (DCB_prime_A_prime_out, in_2, in_3, not_4_out, not_5_out);
  and D_prime_C_prime_B_prime_A_prime (D_prime_C_prime_B_prime_A_prime_out, not_2_out, not_3_out, not_4_out, not_5_out);
  and D_prime_C_prime_BA (D_prime_C_prime_BA_out, not_2_out, not_3_out, in_4, LSB);
  and D_prime_CBA_prime (D_prime_CBA_prime_out, not_2_out, in_3, in_4, not_5_out);
  and DCBA (DCBA_out, in_2, in_3, in_4, LSB);
  and DC_prime_B_prime_A (DC_prime_B_prime_A_out, in_2, not_3_out, not_4_out, LSB);
  and D_prime_CB_prime_A (D_prime_CB_prime_A_out, not_2_out, in_3, not_4_out, LSB);
  and D_prime_C_prime_BA_prime (D_prime_C_prime_BA_prime_out, not_2_out, not_3_out, in_4, not_5_out);
  and DCBA_prime (DCBA_prime_out, in_2, in_3, in_4, not_5_out);
  and DC_prime_BA (DC_prime_BA_out, in_2, not_3_out, in_4, LSB);
  and DC_prime_B_prime_A_prime (DC_prime_B_prime_A_prime_out, in_2, not_3_out, not_4_out, not_5_out);
  or or_1 (or_1_out, DCB_prime_A_prime_out, or_2_out);
  or or_2 (or_2_out, D_prime_C_prime_B_prime_A_prime_out, D_prime_C_prime_BA_out, D_prime_CBA_prime_out, DCBA_out, DC_prime_B_prime_A_out);
  and and_1 (and_1_out, MSB, or_3_out);
  or or_3 (or_3_out, D_prime_CB_prime_A_out, D_prime_C_prime_BA_prime_out, DCBA_prime_out, DC_prime_BA_out, DC_prime_B_prime_A_prime_out);
  and and_2 (and_2_out, not_1_out, or_1_out);
  or or_4 (out_6, and_2_out, and_1_out);

  // Notes on the sheet:
  //   E
  //   C
  //   D
  //   B
  //   A
endmodule

module a__Ones_7_seg (
  input  MSB,
  input  in_2,
  input  in_3,
  input  in_4,
  input  LSB,
  output out_6
);

  wire and_1_out, and_2_out, BA_prime_out, C_prime_A_out, C_prime_A_prime_out, CA_out, D_prime_A_prime_out,
       D_prime_B_2_out, D_prime_B_out, DB_prime_out, DCB_prime_out, not_1_out, not_2_out, not_3_out,
       not_4_out, not_5_out, or_1_out, or_2_out;

  not not_1 (not_1_out, MSB);
  not not_2 (not_2_out, in_2);
  not not_3 (not_3_out, in_3);
  not not_4 (not_4_out, in_4);
  not not_5 (not_5_out, LSB);
  and C_prime_A_prime (C_prime_A_prime_out, not_3_out, not_5_out);
  and DB_prime (DB_prime_out, in_2, not_4_out);
  and CA (CA_out, in_3, LSB);
  and D_prime_B (D_prime_B_out, not_2_out, in_4);
  and DCB_prime (DCB_prime_out, in_2, in_3, not_4_out);
  and D_prime_A_prime (D_prime_A_prime_out, not_2_out, not_5_out);
  and C_prime_A (C_prime_A_out, not_3_out, LSB);
  and D_prime_B_2 (D_prime_B_2_out, not_2_out, in_4);
  and BA_prime (BA_prime_out, in_4, not_5_out);
  or or_1 (or_1_out, C_prime_A_prime_out, DB_prime_out, CA_out, D_prime_B_out);
  or or_2 (or_2_out, DCB_prime_out, D_prime_A_prime_out, C_prime_A_out, D_prime_B_2_out, BA_prime_out);
  and and_1 (and_1_out, not_1_out, or_1_out);
  and and_2 (and_2_out, MSB, or_2_out);
  or or_3 (out_6, and_1_out, and_2_out);

  // Notes on the sheet:
  //   D
  //   E
  //   B
  //   C
  //   A
  //   a (ones 7-seg)
  //   E'(C'A'+DB'+CA+D'B)
  //   E(DCB'+D'A'+C'A+D'B+BA')
endmodule

module b__Ones_7_seg (
  input  MSB,
  input  in_2,
  input  in_3,
  input  in_4,
  input  LSB,
  output out_6
);

  wire and_1_out, and_2_out, B_prime_A_prime_out, BA_out, D_prime_A_out, D_prime_B_out, D_prime_BA_out,
       DA_prime_out, DB_prime_A_prime_out, DB_prime_out, not_1_out, not_2_out, not_3_out, not_4_out,
       not_5_out, or_1_out, or_2_out;

  not not_1 (not_1_out, MSB);
  not not_2 (not_2_out, in_2);
  not not_3 (not_3_out, in_4);
  not not_4 (not_4_out, in_3);
  not not_5 (not_5_out, LSB);
  and B_prime_A_prime (B_prime_A_prime_out, not_3_out, not_5_out);
  and D_prime_BA (D_prime_BA_out, not_2_out, in_4, LSB);
  and DB_prime (DB_prime_out, in_2, not_3_out);
  and DA_prime (DA_prime_out, in_2, not_5_out);
  and D_prime_A (D_prime_A_out, not_2_out, LSB);
  and D_prime_B (D_prime_B_out, not_2_out, in_4);
  and DB_prime_A_prime (DB_prime_A_prime_out, in_2, not_3_out, not_5_out);
  and BA (BA_out, in_4, LSB);
  or or_1 (or_1_out, not_4_out, B_prime_A_prime_out, D_prime_BA_out, DB_prime_out, DA_prime_out);
  and and_1 (and_1_out, not_1_out, or_1_out);
  and and_2 (and_2_out, MSB, or_2_out);
  or or_2 (or_2_out, in_3, D_prime_A_out, D_prime_B_out, DB_prime_A_prime_out, BA_out);
  or or_3 (out_6, and_1_out, and_2_out);

  // Notes on the sheet:
  //   E
  //   D
  //   C
  //   B
  //   A
  //   b (ones 7-seg)
  //   E'(B'A'+D'BA+C'+DB'+DA')
  //   E(D'A+D'B+C+DB'A'+BA)
endmodule

module c__Ones_7_seg (
  input  MSB,
  input  D,
  input  in_3,
  input  in_4,
  input  LSB,
  output out_6
);

  wire and_1_out, and_2_out, CB_out, D_prime_B_prime_out, D_prime_C_prime_out, DC_prime_out, not_1_out,
       not_2_out, not_3_out, not_4_out, or_1_out, or_2_out;

  not not_1 (not_1_out, MSB);
  not not_2 (not_2_out, D);
  not not_3 (not_3_out, in_3);
  not not_4 (not_4_out, in_4);
  and D_prime_B_prime (D_prime_B_prime_out, not_2_out, not_4_out);
  and CB (CB_out, in_3, in_4);
  and DC_prime (DC_prime_out, D, not_3_out);
  and D_prime_C_prime (D_prime_C_prime_out, not_2_out, not_3_out);
  or or_1 (or_1_out, not_4_out, D, D_prime_C_prime_out);
  and and_1 (and_1_out, not_1_out, or_2_out);
  or or_2 (or_2_out, D_prime_B_prime_out, CB_out, DC_prime_out);
  and and_2 (and_2_out, MSB, or_1_out);
  or or_3 (out_6, and_1_out, and_2_out, LSB);

  // Notes on the sheet:
  //   E
  //   C
  //   B
  //   A
  //   c (ones 7-seg)
  //   E'(D'B'+CB+DC')
  //   E(B'+D'C'+D)
endmodule

module d__Ones_7_seg (
  input  MSB,
  input  in_2,
  input  in_3,
  input  in_4,
  input  LSB,
  output out_6
);

  wire and_1_out, and_2_out, BA_prime_out, C_prime_A_prime_out, CA_prime_out, CB_prime_A_out,
       D_prime_A_prime_out, D_prime_B_out, D_prime_BA_prime_out, D_prime_C_prime_B_out, DB_prime_A_out,
       DB_prime_out, DCA_out, not_1_out, not_2_out, not_3_out, not_4_out, not_5_out, or_1_out, or_2_out,
       or_3_out;

  not not_1 (not_1_out, MSB);
  not not_2 (not_2_out, in_2);
  not not_3 (not_3_out, in_4);
  not not_4 (not_4_out, in_3);
  not not_5 (not_5_out, LSB);
  and DB_prime (DB_prime_out, in_2, not_3_out);
  and C_prime_A_prime (C_prime_A_prime_out, not_4_out, not_5_out);
  and CB_prime_A (CB_prime_A_out, in_3, not_3_out, LSB);
  and D_prime_C_prime_B (D_prime_C_prime_B_out, not_2_out, not_4_out, in_4);
  and D_prime_BA_prime (D_prime_BA_prime_out, not_2_out, in_4, not_5_out);
  and DCA (DCA_out, in_2, in_3, LSB);
  and D_prime_A_prime (D_prime_A_prime_out, not_2_out, not_5_out);
  and CA_prime (CA_prime_out, in_3, not_5_out);
  and DB_prime_A (DB_prime_A_out, in_2, not_3_out, LSB);
  and D_prime_B (D_prime_B_out, not_2_out, in_4);
  and BA_prime (BA_prime_out, in_4, not_5_out);
  or or_1 (or_1_out, DB_prime_out, C_prime_A_prime_out, CB_prime_A_out, D_prime_C_prime_B_out, D_prime_BA_prime_out);
  or or_2 (or_2_out, or_1_out, DCA_out);
  or or_3 (or_3_out, D_prime_A_prime_out, CA_prime_out, DB_prime_A_out, D_prime_B_out, BA_prime_out);
  and and_1 (and_1_out, not_1_out, or_2_out);
  and and_2 (and_2_out, MSB, or_3_out);
  or or_4 (out_6, and_1_out, and_2_out);

  // Notes on the sheet:
  //   E
  //   C
  //   D
  //   B
  //   A
  //   d (ones 7-seg)
  //   E'(DB'+C'A'+CB'A+D'C'B+D'BA'+DCA)
  //   E(D'A'+CA'+DB'A+D'B+BA')
endmodule

module e__Ones_7_seg (
  input  MSB,
  input  in_2,
  input  in_3,
  input  in_4,
  input  LSB,
  output out_6
);

  wire and_1_out, and_2_out, D_prime_B_out, DB_prime_out, E_prime_A_prime_out, EA_prime_out, EB_out, EC_out,
       not_1_out, not_2_out, not_3_out, not_4_out, not_5_out, or_1_out, or_2_out;

  not not_1 (not_1_out, MSB);
  not not_2 (not_2_out, in_2);
  not not_3 (not_3_out, in_4);
  not not_4 (not_4_out, in_3);
  not not_5 (not_5_out, LSB);
  and E_prime_A_prime (E_prime_A_prime_out, not_1_out, not_5_out);
  and DB_prime (DB_prime_out, in_2, not_3_out);
  and D_prime_B (D_prime_B_out, not_2_out, in_4);
  and EA_prime (EA_prime_out, MSB, not_5_out);
  and EC (EC_out, MSB, in_3);
  and EB (EB_out, MSB, in_4);
  or or_1 (or_1_out, DB_prime_out, D_prime_B_out, not_4_out);
  or or_2 (or_2_out, EC_out, EB_out, not_2_out);
  and and_1 (and_1_out, E_prime_A_prime_out, or_1_out);
  and and_2 (and_2_out, EA_prime_out, or_2_out);
  or or_3 (out_6, and_1_out, and_2_out);

  // Notes on the sheet:
  //   E
  //   D
  //   C
  //   B
  //   A
  //   e (ones 7-seg)
  //   E'A'(C'+DB'+D'B)
  //   EA'(D'+EC+EB)
endmodule

module f__Ones_7_seg (
  input  MSB,
  input  in_2,
  input  in_3,
  input  in_4,
  input  LSB,
  output out_6
);

  wire and_1_out, and_2_out, B_prime_A_prime_out, CBA_prime_out, D_prime_B_prime_A_prime_out,
       D_prime_C_prime_B_out, D_prime_CB_prime_out, DB_prime_out, DBA_prime_2_out, DBA_prime_out,
       DC_prime_B_prime_out, DCB_out, not_1_out, not_2_out, not_3_out, not_4_out, not_5_out, or_1_out,
       or_2_out, or_3_out;

  not not_1 (not_1_out, MSB);
  not not_2 (not_2_out, in_2);
  not not_3 (not_3_out, in_4);
  not not_4 (not_4_out, in_3);
  not not_5 (not_5_out, LSB);
  and DC_prime_B_prime (DC_prime_B_prime_out, in_2, not_4_out, not_3_out);
  and D_prime_B_prime_A_prime (D_prime_B_prime_A_prime_out, not_2_out, not_3_out, not_5_out);
  and D_prime_CB_prime (D_prime_CB_prime_out, not_2_out, in_3, not_3_out);
  and DCB (DCB_out, in_2, in_3, in_4);
  and CBA_prime (CBA_prime_out, in_3, in_4, not_5_out);
  and DBA_prime (DBA_prime_out, in_2, in_4, not_5_out);
  and B_prime_A_prime (B_prime_A_prime_out, not_3_out, not_5_out);
  and DB_prime (DB_prime_out, in_2, not_3_out);
  and D_prime_C_prime_B (D_prime_C_prime_B_out, not_2_out, not_4_out, in_4);
  and DBA_prime_2 (DBA_prime_2_out, in_2, in_4, not_5_out);
  or or_1 (or_1_out, DC_prime_B_prime_out, D_prime_B_prime_A_prime_out, D_prime_CB_prime_out, DCB_out, CBA_prime_out);
  or or_2 (or_2_out, B_prime_A_prime_out, DB_prime_out, D_prime_C_prime_B_out, DBA_prime_2_out);
  and and_1 (and_1_out, not_1_out, or_3_out);
  or or_3 (or_3_out, or_1_out, DBA_prime_out);
  and and_2 (and_2_out, MSB, or_2_out);
  or or_4 (out_6, and_1_out, and_2_out);

  // Notes on the sheet:
  //   E
  //   C
  //   D
  //   B
  //   A
  //   f (ones 7-seg)
  //   E'(DC'B+DB'A'+D'CB'+DCB+CBA+DBA')
  //   E(B'A'+DB'+D'C'B+DBA')
endmodule

module g__Ones_7_seg (
  input  MSB,
  input  D,
  input  C,
  input  in_4,
  input  LSB,
  output out_6
);

  wire and_1_out, and_2_out, C_prime_A_prime_out, CB_prime_out, CBA_prime_out, D_prime_B_out,
       D_prime_C_prime_B_out, DB_prime_out, DC_out, not_1_out, not_2_out, not_3_out, not_4_out, not_5_out,
       or_1_out, or_2_out;

  not not_1 (not_1_out, MSB);
  not not_2 (not_2_out, D);
  not not_3 (not_3_out, in_4);
  not not_4 (not_4_out, C);
  not not_5 (not_5_out, LSB);
  and DB_prime (DB_prime_out, D, not_3_out);
  and CB_prime (CB_prime_out, C, not_3_out);
  and DC (DC_out, D, C);
  and D_prime_C_prime_B (D_prime_C_prime_B_out, not_2_out, not_4_out, in_4);
  and CBA_prime (CBA_prime_out, C, in_4, not_5_out);
  and C_prime_A_prime (C_prime_A_prime_out, not_4_out, not_5_out);
  and D_prime_B (D_prime_B_out, not_2_out, in_4);
  or or_1 (or_1_out, CB_prime_out, DC_out, D_prime_C_prime_B_out, CBA_prime_out);
  or or_2 (or_2_out, C_prime_A_prime_out, D_prime_B_out);
  and and_1 (and_1_out, not_1_out, or_1_out);
  and and_2 (and_2_out, MSB, or_2_out);
  or or_3 (out_6, DB_prime_out, and_1_out, and_2_out);

  // Notes on the sheet:
  //   E
  //   B
  //   A
  //   g (ones 7-seg)
  //   E'(CB'+DC+D'C'B+CBA')
  //   E(C'A'+D'B)
endmodule

module a__Tens_7_seg (
  input  MSB,
  input  in_2,
  input  in_3,
  input  in_4,
  input  LSB,
  output out_6
);

  wire and_1_out, and_2_out, C_prime_B_prime_out, D_C_out, not_1_out, not_2_out, not_3_out, not_4_out,
       or_1_out;

  not not_1 (not_1_out, MSB);
  not not_2 (not_2_out, in_2);
  not not_3 (not_3_out, in_3);
  not not_4 (not_4_out, in_4);
  and C_prime_B_prime (C_prime_B_prime_out, not_3_out, not_4_out);
  or D_C (D_C_out, in_2, in_3);
  or or_1 (or_1_out, C_prime_B_prime_out, not_2_out);
  and and_1 (and_1_out, MSB, D_C_out);
  and and_2 (and_2_out, not_1_out, or_1_out);
  or or_2 (out_6, and_2_out, and_1_out);

  // Notes on the sheet:
  //   E
  //   C
  //   D
  //   B
  //   A
  //   E(D+C)
  //   a (tens 7-seg)
  //   E'(C'B'+D')
endmodule

module c__Tens_7_seg (
  input  MSB,
  input  D,
  input  C,
  input  in_4,
  input  LSB,
  output out_6
);

  wire ED_prime_C_prime_out, EDCB_out, not_1_out, not_2_out, not_3_out;

  not not_1 (not_1_out, MSB);
  not not_2 (not_2_out, D);
  not not_3 (not_3_out, C);
  and ED_prime_C_prime (ED_prime_C_prime_out, MSB, not_2_out, not_3_out);
  and EDCB (EDCB_out, MSB, D, C, in_4);
  or or_1 (out_6, not_1_out, ED_prime_C_prime_out, EDCB_out);

  // Notes on the sheet:
  //   E
  //   B
  //   A
  //   c (tens 7-seg)
endmodule

module d__Tens_7_seg (
  input  MSB,
  input  D,
  input  C,
  input  B,
  input  LSB,
  output out_6
);

  wire and_1_out, and_2_out, C_prime_B_prime_out, D_C_out, not_1_out, not_2_out, not_3_out, not_4_out,
       or_1_out;

  not not_1 (not_1_out, MSB);
  not not_2 (not_2_out, D);
  not not_3 (not_3_out, C);
  not not_4 (not_4_out, B);
  and C_prime_B_prime (C_prime_B_prime_out, not_3_out, not_4_out);
  or D_C (D_C_out, D, C);
  or or_1 (or_1_out, C_prime_B_prime_out, not_2_out);
  and and_1 (and_1_out, MSB, D_C_out);
  and and_2 (and_2_out, not_1_out, or_1_out);
  or or_2 (out_6, and_2_out, and_1_out);

  // Notes on the sheet:
  //   E
  //   A
  //   d (tens 7-seg)
  //   E(D+C)
  //   E'(C'B'+D')
endmodule

module e__Tens_7_seg (
  input  MSB,
  input  D,
  input  C,
  input  in_4,
  input  LSB,
  output out_6
);

  wire and_1_out, and_2_out, C_prime_B_prime_out, D_prime_C_out, DB_prime_out, DC_prime_out, not_1_out,
       not_2_out, not_3_out, not_4_out, or_1_out, or_2_out;

  not not_1 (not_1_out, MSB);
  not not_2 (not_2_out, D);
  not not_3 (not_3_out, C);
  not not_4 (not_4_out, in_4);
  and C_prime_B_prime (C_prime_B_prime_out, not_3_out, not_4_out);
  and DB_prime (DB_prime_out, D, not_4_out);
  and D_prime_C (D_prime_C_out, not_2_out, C);
  and DC_prime (DC_prime_out, D, not_3_out);
  and and_1 (and_1_out, not_1_out, or_1_out);
  or or_1 (or_1_out, C_prime_B_prime_out, not_2_out);
  and and_2 (and_2_out, MSB, or_2_out);
  or or_2 (or_2_out, DB_prime_out, D_prime_C_out, DC_prime_out);
  or or_3 (out_6, and_1_out, and_2_out);

  // Notes on the sheet:
  //   E
  //   B
  //   A
  //   e (tens 7-seg)
  //   E'(C'B'+D')
  //   E(DB'+D'C+DC')
endmodule

module f__Tens_7_seg (
  input  MSB,
  input  D,
  input  C,
  input  B,
  input  LSB,
  output out_6
);

  wire and_1_out, E_prime_D_prime_out, not_1_out, not_2_out, not_3_out, not_4_out;

  not not_1 (not_1_out, MSB);
  not not_2 (not_2_out, D);
  not not_3 (not_3_out, C);
  not not_4 (not_4_out, B);
  // NOT_Gate not_5 has open pins: in=LSB, out=open
  and and_1 (and_1_out, not_1_out, not_3_out, not_4_out);
  and E_prime_D_prime (E_prime_D_prime_out, not_1_out, not_2_out);
  or or_1 (out_6, and_1_out, E_prime_D_prime_out);

  // Notes on the sheet:
  //   E
  //   A
  //   f (tens 7-seg)
  //   E'C'B'
endmodule

module g__Tens_7_seg (
  input  MSB,
  input  in_2,
  input  in_3,
  input  in_4,
  input  LSB,
  output E_D_C
);

  wire D_C_out;

  or D_C (D_C_out, in_2, in_3);
  and and_1 (E_D_C, MSB, D_C_out);

  // Notes on the sheet:
  //   E
  //   D
  //   C
  //   B
  //   A
  //   g (tens 7-seg)
endmodule
